# Fritzing sketch wiring (saved by Fritzing 0.9.3b)

parts:
  Bauteil1 = Arduino Pro Mini (3.3V)
  Config-/Toggle-Taster = Momentary Switch [package=ksa_sealed_tac_switch]
  LED1 = LED - 3mm [color="Green (560nm)" package="3 mm [THT]"]
  R1 = Resistor [tolerance=±5% resistance=330 package=THT]
  R2 = Resistor [tolerance=±5% resistance=1k package=THT]
  X2 = USB Connectors [package=usb-a-s]
  Q1 = Basic FET P-Channel [package="DPak [SMD]"]
  Antenne_~8_3cm = CC1101 [part_number=CC1101]
  X1 = USB Connectors [package=usb-a-h]
  Bauteil2 = INA219 High Side DC Current Sensor Breakout [part_number=904]
  R3 = Resistor [tolerance=±5% resistance=100k package=THT]
  LED2 = LED - 3mm [color="Green (560nm)" package="3 mm [THT]"]
  R4 = Resistor [tolerance=±5% resistance=330 package=THT]

nets:
  N1: Bauteil1.A4, Bauteil2.SDA
  N2: Bauteil1.A5, Bauteil2.SCL
  N3: Bauteil1.RAW, X1.VBUS, Bauteil2.VIN+
  N4: Bauteil1.GND, Config-/Toggle-Taster.4, LED1.cathode, Antenne_~8_3cm.2
  VCC: Bauteil1.VCC, Antenne_~8_3cm.1, Bauteil2.VCC
  N5: Bauteil1.SCK, Antenne_~8_3cm.4
  N6: Bauteil1.MISO, Antenne_~8_3cm.5
  N7: Bauteil1.MOSI, Antenne_~8_3cm.3
  N8: Bauteil1.D10, Antenne_~8_3cm.8
  N9: Bauteil1.D8, Config-/Toggle-Taster.3
  N10: Bauteil1.D6, R2.Pin_0, R4.Pin_1
  N11: Bauteil1.D4, R1.Pin_0
  N12: Bauteil1.D2, Antenne_~8_3cm.7
  N13: LED1.anode, R1.Pin_1
  N14: X2.GND, LED2.cathode
  N15: X2.VBUS, Q1.drain, R3.Pin_0
  N16: Q1.source, Bauteil2.VIN-
  GND: X1.GND, Bauteil2.GND
  N17: LED2.anode, R4.Pin_0

notes:
  "Output On" LED
  (optional)

custom parts:
  INA219 High Side DC Current Sensor Breakout: This breakout board will solve all your power-monitoring problems. Instead of struggling with two multimeters, you can just use the handy INA219B chip on this breakout to both measure both the high side voltage and DC current draw over I2C with 1% precision. Most current-measuring devices such as our current panel meter are only good for low side measuring. That means that unless you want to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
